# Fritzing sketch 555Blink (saved by Fritzing 0.9.3b)
breadboards: 1

parts:
  U1 = 555 Timer [package="DIP8 [THT]"]
  C2 = Electrolytic Capacitor [capacitance=10µF package="0405 [SMD, electrolytic]"]
  R1 = Resistor [tolerance=±5% resistance=1k package=THT]
  LED1 = LED - 3mm [color="Red (633nm)" package="3 mm [THT]"]
  R3 = Resistor [tolerance=±5% resistance=100k package="0603 [SMD]"]
  R4 = Resistor [tolerance=±5% resistance=1k package="0402 [SMD]"]
  BAT1 = BC9VPC [package=bc9vpc]

nets:
  N1: U1.Pin_1, C2.-, LED1.cathode, BAT1.V-
  N2: U1.Pin_2, U1.Pin_6, C2.+, R3.Pin_0
  N3: U1.Pin_3, R1.Pin_0
  N4: U1.Pin_4, U1.Pin_8, R4.Pin_0, BAT1.V+
  N5: U1.Pin_7, R3.Pin_1, R4.Pin_1
  N6: R1.Pin_1, LED1.anode
